# Fritzing sketch PiezoElectric_sensor (saved by Fritzing 0.9.3b)
breadboards: 1

parts:
  J1 = Piezo Speaker
  Part1 = Arduino Uno (Rev3)
  R1 = Resistor [tolerance=±5% resistance=220 package="0805 [SMD]"]
  R2 = Resistor [tolerance=±5% resistance=2.2M package="0805 [SMD]"]
  LED1 = smd LED [color="Red (633nm)" package="1206 [SMD]"]

nets:
  N1: J1.pin1, Part1.GND, R2.Pin_0, LED1.cathode
  N2: J1.pin2, Part1.A0, R2.Pin_1
  N3: Part1.D13/SCK, R1.Pin_1
  N4: R1.Pin_0, LED1.anode
